# Fritzing sketch Противопожарная сигнализация схема (saved by Fritzing 0.9.3b)
breadboards: 1

parts:
  Часть1 = Arduino Mega 2560 (Rev3)
  PIR2 = PIR sensor

nets:
  5V: Часть1.5V, PIR2.VDD
  GND: Часть1.GND, PIR2.GND
  N1: Часть1.D49, PIR2.SIG
