# Fritzing sketch авополив схема (saved by Fritzing 0.9.3b)
breadboards: 1

parts:
  Часть1 = Arduino Mega 2560 (Rev3)
  Часть2 = Soil Moisture Sensor
  Часть3 = FC-28 Soil Hygrometer Module
  KY-1 = Keyes Relay [package=THT]

nets:
  5V: Часть1.5V, Часть3.VCC, Часть3.AO, KY-1.power
  N1: Часть1.GND, KY-1.ground
  N2: Часть1.D45, KY-1.signal
  N3: Часть1.D51, Часть3.DO
  N4: Часть2.GND, Часть3.NEG
  N5: Часть2.VCC, Часть3.POS

custom parts:
  FC-28 Soil Hygrometer Module: The FC-28 is a soil hygrometer module that uses the Texas Instruments LM393 comparator chip to provide an analog measurement of soil humidity. The digital output is high when soil moisture is over a certain threshold, as determined by adjusting the potentiometer.
  Keyes Relay: The Keyes 5V relay module is suitable for SCM development, home appliance control. It uses a 5V~12V TIL control signal which can control DC / AC signal.
