# Fritzing sketch сигнализация от воров схема (saved by Fritzing 0.9.3b)
breadboards: 1

parts:
  Часть1 = Arduino Mega 2560 (Rev3)
  Часть2 = SRF05 Ultrasonic Rangefinder
  Часть4 = SRF05 Ultrasonic Rangefinder
  KY-1 = Keyes Relay [package=THT]

nets:
  N1: Часть1.D9_PWM, Часть2.Trig
  N2: Часть1.D8_PWM, Часть2.Echo
  VCC: Часть1.5V, Часть2.VCC, Часть4.VCC, KY-1.power
  GND: Часть1.GND, Часть2.GND, Часть4.GND, KY-1.ground
  N3: Часть1.D6_PWM, Часть4.Echo
  N4: Часть1.D7_PWM, Часть4.Trig
  N5: Часть1.D43, KY-1.signal

custom parts:
  Keyes Relay: The Keyes 5V relay module is suitable for SCM development, home appliance control. It uses a 5V~12V TIL control signal which can control DC / AC signal.
